# Fritzing sketch BareBones (saved by Fritzing 1.0.6)
breadboards: 1

parts:
  Part1 = Arduino Uno (Rev3)
  Part2 = Digital Temperature Sensor Breakout - TMP102

nets:
  N1: Part1.A4/SDA, Part2.SDA
  N2: Part1.A5/SCL, Part2.SCL
  N3: Part1.5V, Part2.V+
  GND: Part1.GND, Part2.GND

notes:
  C1
  5V
  GND
  A4/SDA
  A5/SCL
  VCC
  OS
  SCL
  SDA
  NC
  A5
  A4
